// Logisim project AdderSubCircuit.circ as structural Verilog: 1 circuit, main circuit main
module main (
  input  A4,
  input  A3,
  input  A2,
  input  A1
);

  wire n7486_1_pin7, n7486_1_pin14, n74283_1_pin1, n74283_1_pin2, n74283_1_pin4, n74283_1_pin6,
       n74283_1_pin10, n74283_1_pin11, n74283_1_pin13, n74283_1_pin15;

  _7486 #(.ShowInternalStructure("true"), .VccGndPorts("true")) u_7486_1 (
    .pin7(n7486_1_pin7), .pin14(n7486_1_pin14));  // open: pin1, pin2, pin3, pin4, pin5, pin6, pin13, pin12, pin11, pin10, pin9, pin8
  _74283 #(.ShowInternalStructure("true"), .VccGndPorts("true")) u_74283_1 (
    .pin1(n74283_1_pin1), .pin2(n74283_1_pin2), .pin3(A2), .pin4(n74283_1_pin4), .pin5(A1),
    .pin6(n74283_1_pin6), .pin7(n7486_1_pin7), .pin8(n7486_1_pin7), .pin16(n7486_1_pin14),
    .pin15(n74283_1_pin15), .pin14(A3), .pin13(n74283_1_pin13), .pin12(A4), .pin11(n74283_1_pin11),
    .pin10(n74283_1_pin10));  // open: pin9
  LED O3 (.in(n74283_1_pin10));
  LED O2 (.in(n74283_1_pin13));
  LED O1 (.in(n74283_1_pin1));
  LED O0 (.in(n74283_1_pin4));
  // also tied to GND on the sheet: n7486_1_pin7
  // also tied to VCC on the sheet: n7486_1_pin14
endmodule
