// Logisim project LabFinal.circ as structural Verilog: 1 circuit, main circuit main
module main (
  input  A0,
  input  A1,
  input  A2,
  input  A3,
  input  B0,
  input  B1,
  input  B2,
  input  B3,
  input  S0,
  input  S1,
  input  AS
);

  wire n7486_1_pin3, n7486_1_pin6, n74153_1_pin1, n74153_1_pin4, n74153_1_pin5, n74153_1_pin7, n74153_1_pin9,
       n74153_1_pin11, n74153_1_pin12;

  _7486 #(.ShowInternalStructure("true")) u_7486_1 (
    .pin1(A0), .pin2(B0), .pin3(n7486_1_pin3), .pin4(A1), .pin5(B1), .pin6(n7486_1_pin6), .pin13(A3),
    .pin12(B3), .pin10(A2), .pin9(B2));  // open: pin11, pin8
  _74153 #(.ShowInternalStructure("true")) u_74153_1 (
    .pin1(n74153_1_pin1), .pin2(S1), .pin3(n7486_1_pin3), .pin4(n74153_1_pin4), .pin5(n74153_1_pin5),
    .pin6(n74153_1_pin1), .pin7(n74153_1_pin7), .pin15(n74153_1_pin1), .pin14(S0), .pin13(n7486_1_pin6),
    .pin12(n74153_1_pin12), .pin11(n74153_1_pin11), .pin10(n74153_1_pin1), .pin9(n74153_1_pin9));
  _7408 #(.ShowInternalStructure("true")) u_7408_1 (
    .pin1(A0), .pin2(B0), .pin3(n74153_1_pin5), .pin4(A1), .pin5(B1), .pin6(n74153_1_pin11), .pin13(B3),
    .pin12(A3), .pin10(A2), .pin9(B2));  // open: pin11, pin8
  _7432 #(.ShowInternalStructure("true")) u_7432_1 (
    .pin1(A0), .pin2(B0), .pin3(n74153_1_pin4), .pin4(A1), .pin5(B1), .pin6(n74153_1_pin12), .pin13(A3),
    .pin12(B3), .pin10(A2), .pin9(B2));  // open: pin11, pin8
  LED O0 (.in(n74153_1_pin7));
  LED O1 (.in(n74153_1_pin9));
  LED O2 ();  // open: in
  LED O3 ();  // open: in
  // also tied to GND on the sheet: n74153_1_pin1
endmodule
